# Fritzing sketch voiture_ir (saved by Fritzing 0.9.3b)

parts:
  Composant1 = Arduino Uno (Rev3)
  S1 = H-Bridge with L298N
  hc-sr1 = hc-sr04
  Keyes1 = Keyes IR Infrared Sensor Switch Module
  VCC1 = Battery
  IR1 = TSOP312.., 314.. [package=THT]

nets:
  N1: Composant1.D8, hc-sr1.Trig
  GND: Composant1.D9_PWM, Composant1.GND, S1.GND, hc-sr1.Echo, hc-sr1.GND, Keyes1.GND, VCC1.-, IR1.GND
  N2: Composant1.D10_PWM/SS, Keyes1.out
  N3: Composant1.D2, IR1.Data
  N4: Composant1.D3_PWM, S1.IN1
  N5: Composant1.D4, S1.IN2
  N6: Composant1.D5_PWM, S1.IN3
  N7: Composant1.D6_PWM, S1.IN4
  VCC: Composant1.5V, hc-sr1.VCC, Keyes1.VCC, IR1.Vs
  VIN: Composant1.VIN, S1.12V, VCC1.+

custom parts:
  H-Bridge with L298N: h-bridge
  Keyes IR Infrared Sensor Switch Module: An infrared obstacle detector
